// Logisim project trab.circ as structural Verilog: 3 circuits, main circuit main
module main (
);

  wire and_1_out, button_1_out, CLK, CONTROL_UNIT_add, CONTROL_UNIT_rdm, HLT, not_1_out, not_2_out,
       not_3_out, STR;
  wire [1:0] CONTROL_UNIT_regaddr0, CONTROL_UNIT_regaddr1, RAMADDR;
  wire [4:0] counter_1_q;
  wire [7:0] ram_1_data, RAMIN, RAMOUT, rom_1_data;

  Clock clock_1 (.out(CLK));
  Counter #(.width(5), .max('h1f)) counter_1 (
    .Q(counter_1_q), .clk(and_1_out), .clr(button_1_out));  // open: load, D, count, carry
  and and_1 (and_1_out, not_1_out, CLK);
  not not_1 (not_1_out, HLT);
  not not_2 (not_2_out, STR);
  Button button_1 (.out(button_1_out));
  RAM #(.addrWidth(2), .bus("asynch")) ram_1 (.addr(RAMADDR), .data(ram_1_data), .ld(not_2_out));  // open: sel, clr
  not not_3 (not_3_out, STR);
  assign RAMOUT = not_3_out ? ram_1_data : 8'bz;  // Controlled_Buffer controlled_buffer_1
  assign ram_1_data = STR ? RAMIN : 8'bz;  // Controlled_Buffer controlled_buffer_2
  ROM #(.addrWidth(5)) rom_1 (.addr(counter_1_q), .data(rom_1_data));  // open: sel
  assign RAMOUT = STR ? {8{1'b0}} : 8'bz;  // Controlled_Buffer controlled_buffer_3
  Register INSTRUCTION_REGISTER (.D(rom_1_data), .clk(CLK));  // open: en, Q, clr
  CONTROL_UNIT CONTROL_UNIT (
    .INSTR(rom_1_data), .RDM(CONTROL_UNIT_rdm), .REGADDR0(CONTROL_UNIT_regaddr0),
    .REGADDR1(CONTROL_UNIT_regaddr1), .RAMADDR(RAMADDR), .STR(STR), .HLT(HLT), .ADD(CONTROL_UNIT_add));
  ALU ALU (
    .RDM(CONTROL_UNIT_rdm), .STR(STR), .ADD(CONTROL_UNIT_add), .REGADRR0(CONTROL_UNIT_regaddr0),
    .REGADRR1(CONTROL_UNIT_regaddr1), .RAMOUT(RAMOUT), .CLK(CLK), .REGOUT(RAMIN));

  // Notes on the sheet:
  //   RAM
  //   ROM
  //   contents of rom_1 (hex, n*v repeats v):
  //   d0 d5 da df e3 e6 e9 ec 0 84
endmodule

module CONTROL_UNIT (
  input  [7:0] INSTR,
  output RDM,
  output [1:0] REGADDR0,
  output [1:0] REGADDR1,
  output [1:0] RAMADDR,
  output STR,
  output HLT,
  output ADD
);

  wire and_1_out, and_2_out, and_3_out, and_4_out, and_5_out, and_6_out, and_7_out, and_8_out, not_1_out,
       not_2_out, not_3_out, not_4_out, not_5_out, not_6_out, not_7_out;

  and and_1 (and_1_out, INSTR[7], INSTR[6]);
  and and_2 (and_2_out, INSTR[7], INSTR[6]);
  and and_3 (and_3_out, INSTR[7], not_1_out);
  not not_1 (not_1_out, INSTR[6]);
  and and_4 (and_4_out, INSTR[7], not_2_out);
  not not_2 (not_2_out, INSTR[6]);
  not not_3 (not_3_out, INSTR[5]);
  and and_5 (and_5_out, and_2_out, INSTR[5]);
  and and_6 (and_6_out, and_3_out, not_4_out);
  not not_4 (not_4_out, INSTR[5]);
  and and_7 (and_7_out, and_4_out, not_5_out);
  not not_5 (not_5_out, INSTR[5]);
  and and_8 (and_8_out, and_1_out, not_3_out);
  and and_9 (RDM, and_8_out, INSTR[4]);
  and and_10 (STR, and_5_out, not_6_out);
  not not_6 (not_6_out, INSTR[4]);
  and and_11 (HLT, and_6_out, not_7_out);
  not not_7 (not_7_out, INSTR[4]);
  and and_12 (ADD, and_7_out, INSTR[4]);
  assign REGADDR1 = ADD ? INSTR[1:0] : 2'bz;  // Controlled_Buffer controlled_buffer_1
  assign REGADDR0 = STR ? INSTR[3:2] : 2'bz;  // Controlled_Buffer controlled_buffer_2
  assign REGADDR0 = RDM ? INSTR[3:2] : 2'bz;  // Controlled_Buffer controlled_buffer_3
  assign RAMADDR = STR ? INSTR[1:0] : 2'bz;  // Controlled_Buffer controlled_buffer_4
  assign RAMADDR = RDM ? INSTR[1:0] : 2'bz;  // Controlled_Buffer controlled_buffer_5
endmodule

module ALU (
  input  RDM,
  input  STR,
  input  ADD,
  input  [1:0] REGADRR0,
  input  [1:0] REGADRR1,
  input  [7:0] RAMOUT,
  input  CLK,
  output [7:0] REGOUT
);

  wire and_1_out, and_2_out, and_3_out, and_4_out, and_5_out, and_6_out, and_7_out, and_8_out, and_9_out,
       not_1_out, not_2_out, not_3_out, not_4_out, not_5_out, not_6_out, or_1_out;
  wire [1:0] controlled_buffer_1_out;
  wire [7:0] controlled_buffer_2_out, controlled_buffer_5_out, controlled_buffer_7_out,
       controlled_buffer_13_out, REG00OUT, REG01OUT, REG10OUT, REG11OUT, register_1_q, register_2_q,
       register_3_q, register_4_q;

  assign controlled_buffer_1_out = or_1_out ? REGADRR0 : 2'bz;  // Controlled_Buffer controlled_buffer_1
  not not_1 (not_1_out, or_1_out);
  not not_2 (not_2_out, RDM);
  or or_1 (or_1_out, STR, RDM);
  and and_1 (and_1_out, and_3_out, RDM);
  assign controlled_buffer_2_out = and_1_out ? RAMOUT : 8'bz;  // Controlled_Buffer controlled_buffer_2
  assign controlled_buffer_1_out = and_2_out ? 2'b00 : 2'bz;  // Controlled_Buffer controlled_buffer_3
  and and_2 (and_2_out, not_1_out, not_2_out);
  Register register_1 (.D(controlled_buffer_2_out), .Q(register_1_q), .clk(CLK));  // open: en, clr
  assign REG00OUT = and_3_out ? register_1_q : 8'bz;  // Controlled_Buffer controlled_buffer_4
  not not_3 (not_3_out, controlled_buffer_1_out[1]);
  not not_4 (not_4_out, controlled_buffer_1_out[0]);
  and and_3 (and_3_out, not_3_out, not_4_out);
  and and_4 (and_4_out, and_5_out, RDM);
  Register register_2 (.D(controlled_buffer_5_out), .Q(register_2_q), .clk(CLK));  // open: en, clr
  assign controlled_buffer_5_out = and_4_out ? RAMOUT : 8'bz;  // Controlled_Buffer controlled_buffer_5
  and and_5 (and_5_out, controlled_buffer_1_out[0], not_5_out);
  not not_5 (not_5_out, controlled_buffer_1_out[1]);
  assign REG01OUT = and_5_out ? register_2_q : 8'bz;  // Controlled_Buffer controlled_buffer_6
  and and_6 (and_6_out, and_7_out, RDM);
  assign controlled_buffer_7_out = and_6_out ? RAMOUT : 8'bz;  // Controlled_Buffer controlled_buffer_7
  not not_6 (not_6_out, controlled_buffer_1_out[0]);
  and and_7 (and_7_out, not_6_out, controlled_buffer_1_out[1]);
  assign REG10OUT = and_7_out ? register_3_q : 8'bz;  // Controlled_Buffer controlled_buffer_8
  Register register_3 (.D(controlled_buffer_7_out), .Q(register_3_q), .clk(CLK));  // open: en, clr
  assign REGOUT = STR ? REG00OUT : 8'bz;  // Controlled_Buffer controlled_buffer_9
  and and_8 (and_8_out, controlled_buffer_1_out[1], controlled_buffer_1_out[0]);
  assign REGOUT = STR ? REG01OUT : 8'bz;  // Controlled_Buffer controlled_buffer_10
  assign REGOUT = STR ? REG10OUT : 8'bz;  // Controlled_Buffer controlled_buffer_11
  assign REGOUT = STR ? REG11OUT : 8'bz;  // Controlled_Buffer controlled_buffer_12
  and and_9 (and_9_out, and_8_out, RDM);
  assign controlled_buffer_13_out = and_9_out ? RAMOUT : 8'bz;  // Controlled_Buffer controlled_buffer_13
  Register register_4 (.D(controlled_buffer_13_out), .Q(register_4_q), .clk(CLK));  // open: en, clr
  assign REG11OUT = and_8_out ? register_4_q : 8'bz;  // Controlled_Buffer controlled_buffer_14
endmodule
